# Fritzing sketch Simon_Says_v1.5 (saved by Fritzing 0.7.12b)
breadboards: 1

parts:
  ( = IC, DIP package, 14 pins [chip_label=IC spacing=300mil]
  BLUE = LED - 3mm [color="Blue (430nm)" package="3 mm [THT]"]
  S1 = Pushbutton [package="[THT]"]
  RED = LED - 3mm [color="Red (633nm)" package="3 mm [THT]"]
  YELLOW = LED - 3mm [color="Yellow (574nm)" package="3 mm [THT]"]
  S4 = Pushbutton [package="[THT]"]
  GREEN = LED - 3mm [color="Green (555nm)" package="3 mm [THT]"]
  R1 = Resistor [tolerance=±5% resistance=220 package=THT]
  S3 = Pushbutton [package="[THT]"]
  S2 = Pushbutton [package="[THT]"]
  +- = female pin header, 2 pins [form="♀ (female)"]
  R2 = Resistor [tolerance=±5% resistance=10k package=THT]
  R4 = Resistor [tolerance=±5% resistance=10k package=THT]
  R6 = Resistor [tolerance=±5% resistance=10k package=THT]
  R8 = Resistor [tolerance=±5% resistance=10k package=THT]
  R3 = Resistor [tolerance=±5% resistance=220 package=THT]
  R5 = Resistor [tolerance=±5% resistance=220 package=THT]
  R7 = Resistor [tolerance=±5% resistance=220 package=THT]
  POWER = LED - 3mm [color="Red (633nm)" package="3 mm [THT]"]
  R9 = Resistor [tolerance=±5% resistance=220 package=THT]
  + = Piezo Buzzer (Round)

nets:
  N1: (.pin1, BLUE.anode, S1.Pin_3, S1.Pin_4, RED.anode, YELLOW.anode, S4.Pin_3, S4.Pin_4, GREEN.anode, S3.Pin_3, S3.Pin_4, S2.Pin_3, S2.Pin_4, +-.pin2, R9.Pin_0, +.pin1
  N2: (.pin5, +.pin2
  N3: (.pin6, R7.Pin_1
  N4: (.pin7, R5.Pin_1
  N5: (.pin8, R3.Pin_1
  N6: (.pin9, R1.Pin_1
  N7: (.pin10, S4.Pin_1, S4.Pin_2, R8.Pin_1
  N8: (.pin11, S3.Pin_1, S3.Pin_2, R6.Pin_1
  N9: (.pin12, S2.Pin_1, S2.Pin_2, R4.Pin_1
  N10: (.pin13, S1.Pin_1, S1.Pin_2, R2.Pin_1
  N11: (.pin14, +-.pin1, R2.Pin_0, R4.Pin_0, R6.Pin_0, R8.Pin_0, POWER.cathode
  N12: BLUE.cathode, R7.Pin_0
  N13: RED.cathode, R1.Pin_0
  N14: YELLOW.cathode, R3.Pin_0
  N15: GREEN.cathode, R5.Pin_0
  N16: POWER.anode, R9.Pin_1

notes:
  Simon Says v1.5
  -
  +
  ATTINY44/84
  BUZZER

custom parts:
  Piezo Buzzer (Round): Piezo
